// Logisim project traffic_controller.circ as structural Verilog: 1 circuit, main circuit main
module main (
  input  in_1
);

  wire and_1_out, and_2_out, and_4_out, and_5_out, and_10_out, and_12_out, and_13_out, and_15_out, Clk,
       d_ff_1_qn, d_ff_2_qn, d_ff_3_qn, d_ff_4_qn, d_ff_5_qn, d_ff_6_qn, FLASOR, KIRMIZI1, KIRMIZI2,
       KIRMIZI3, KIRMIZI4, not_1_out, not_2_out, not_5_out, not_7_out, Q1, Q2, Q3, Q4, Q5, SAG_OUT_1,
       SAG_OUT_2, SAG_OUT_3, SAG_OUT_4, SARI1, SARI2, SARI3, SARI4, SARI_VAKTI, YESIL1, YESIL2, YESIL3,
       YESIL4, YOL1_AKTIF, YOL2_AKTIF, YOL3_AKTIF, YOL4_AKTIF;

  Clock clock_1 (.out(Clk));
  D_Flip_Flop d_ff_1 (.D(d_ff_1_qn), .clk(d_ff_2_qn), .Q(Q5), .Qn(d_ff_1_qn));  // open: preset, reset
  D_Flip_Flop d_ff_2 (.D(d_ff_2_qn), .clk(d_ff_3_qn), .Q(Q4), .Qn(d_ff_2_qn));  // open: preset, reset
  D_Flip_Flop d_ff_3 (.D(d_ff_3_qn), .clk(d_ff_4_qn), .Q(Q3), .Qn(d_ff_3_qn));  // open: preset, reset
  Decoder #(.select(2)) decoder_1 (
    .out0(YOL1_AKTIF), .out1(YOL2_AKTIF), .out2(YOL3_AKTIF), .out3(YOL4_AKTIF), .sel({Q5, Q4}));  // open: en
  not not_1 (not_1_out, SARI_VAKTI);
  D_Flip_Flop d_ff_4 (.D(d_ff_4_qn), .clk(d_ff_5_qn), .Q(Q2), .Qn(d_ff_4_qn));  // open: preset, reset
  not not_2 (not_2_out, SARI_VAKTI);
  and and_1 (and_1_out, YOL4_AKTIF, SARI_VAKTI);
  not not_3 (KIRMIZI2, YOL2_AKTIF);
  and and_2 (and_2_out, YOL1_AKTIF, SARI_VAKTI);
  not not_4 (KIRMIZI1, YOL1_AKTIF);
  and and_3 (YESIL2, YOL2_AKTIF, not_1_out);
  and and_4 (and_4_out, YOL2_AKTIF, SARI_VAKTI);
  and and_5 (and_5_out, YOL1_AKTIF, SARI_VAKTI);
  D_Flip_Flop d_ff_5 (.D(d_ff_5_qn), .clk(d_ff_6_qn), .Q(Q1), .Qn(d_ff_5_qn));  // open: preset, reset
  and and_6 (YESIL1, YOL1_AKTIF, not_2_out);
  LED led_1 (.in(SAG_OUT_4));
  or or_1 (SARI1, and_2_out, and_1_out);
  or or_2 (SARI2, and_4_out, and_5_out);
  LED led_2 (.in(KIRMIZI4));
  LED led_3 (.in(SARI4));
  LED led_4 (.in(YESIL4));
  and and_7 (SAG_OUT_2, FLASOR, 1'b1);
  D_Flip_Flop d_ff_6 (.D(d_ff_6_qn), .clk(Clk), .Q(FLASOR), .Qn(d_ff_6_qn));  // open: preset, reset
  and and_8 (SAG_OUT_1, FLASOR, 1'b1);
  LED led_5 (.in(KIRMIZI3));
  LED led_6 (.in(SARI3));
  LED led_7 (.in(YESIL3));
  LED led_8 (.in(KIRMIZI1));
  LED led_9 (.in(SARI1));
  LED led_10 (.in(YESIL1));
  and and_9 (SARI_VAKTI, FLASOR, Q1, Q2, Q3);
  LED led_11 (.in(SAG_OUT_1));
  LED led_12 (.in(KIRMIZI2));
  LED led_13 (.in(SARI2));
  LED led_14 (.in(YESIL2));
  LED led_15 (.in(SAG_OUT_3));
  LED led_16 (.in(SAG_OUT_2));
  not not_5 (not_5_out, SARI_VAKTI);
  not not_6 (KIRMIZI3, YOL3_AKTIF);
  not not_7 (not_7_out, SARI_VAKTI);
  and and_10 (and_10_out, YOL3_AKTIF, SARI_VAKTI);
  not not_8 (KIRMIZI4, YOL4_AKTIF);
  and and_11 (YESIL3, YOL3_AKTIF, not_5_out);
  and and_12 (and_12_out, YOL3_AKTIF, SARI_VAKTI);
  and and_13 (and_13_out, YOL2_AKTIF, SARI_VAKTI);
  and and_14 (YESIL4, YOL4_AKTIF, not_7_out);
  and and_15 (and_15_out, YOL4_AKTIF, SARI_VAKTI);
  or or_3 (SARI4, and_15_out, and_10_out);
  or or_4 (SARI3, and_12_out, and_13_out);
  and and_16 (SAG_OUT_4, FLASOR, 1'b1);
  and and_17 (SAG_OUT_3, FLASOR, 1'b1);

  // Other names for the same wires on the sheet: Q0 = FLASOR; R = in_1
endmodule
